# Fritzing sketch ThatPiHunt (saved by Fritzing 0.9.3b)
breadboards: 1

parts:
  LED1 = Super Flux RGB LED (com. anode) [color=Blue]
  R1 = Resistor [tolerance=±5% resistance=220 package=THT]
  R2 = Resistor [tolerance=±5% resistance=330 package=THT]
  R3 = Resistor [tolerance=±5% resistance=330 package=THT]
  S1 = Pushbutton [package="[THT]"]  # not connected
  Raspberry_Pi_1 = Raspberry Pi 3 [part_number=RPI-3-V1.2]

nets:
  N1: LED1.red_cathode, R1.Pin_0
  N2: LED1.blue_cathode, R3.Pin_0
  N3: LED1.green_cathode, Raspberry_Pi_1.3v3
  N4: LED1.common_anode, R2.Pin_0
  N5: R1.Pin_1, Raspberry_Pi_1.GPIO5
  N6: R2.Pin_1, Raspberry_Pi_1.GPIO6
  N7: R3.Pin_1, Raspberry_Pi_1.GPIO13

notes:
  As you can see, the LED is rotated to place each pin in
  a 'lane' by itself. When you place the LED into the breadboard, the 'cutoff' corner should point 'upward' in this picture.
